// Logisim project 3.circ as structural Verilog: 1 circuit, main circuit main
module main (
  input  A3,
  input  B3,
  input  A2,
  input  B2,
  input  A1,
  input  B1,
  input  A0,
  input  B0,
  input  C0,
  output C,
  output S3,
  output S2,
  output S1,
  output S0
);

  wire and_1_out, and_2_out, and_3_out, and_4_out, and_5_out, and_6_out, and_7_out, and_8_out, and_9_out,
       and_10_out, and_11_out, and_12_out, or_2_out, or_3_out, or_4_out, xor_1_out, xor_2_out, xor_3_out,
       xor_4_out;

  and and_1 (and_1_out, A3, B3);
  and and_2 (and_2_out, A3, or_2_out);
  and and_3 (and_3_out, B3, or_2_out);
  and and_4 (and_4_out, A2, B2);
  and and_5 (and_5_out, A2, or_3_out);
  and and_6 (and_6_out, B2, or_3_out);
  and and_7 (and_7_out, A1, B1);
  and and_8 (and_8_out, A1, or_4_out);
  and and_9 (and_9_out, B1, or_4_out);
  and and_10 (and_10_out, A0, B0);
  and and_11 (and_11_out, A0, C0);
  and and_12 (and_12_out, B0, C0);
  xor xor_1 (xor_1_out, A3, B3);
  or or_1 (C, and_1_out, and_2_out, and_3_out);
  xor xor_2 (xor_2_out, A2, B2);
  or or_2 (or_2_out, and_4_out, and_5_out, and_6_out);
  xor xor_3 (xor_3_out, A1, B1);
  or or_3 (or_3_out, and_7_out, and_8_out, and_9_out);
  xor xor_4 (xor_4_out, A0, B0);
  or or_4 (or_4_out, and_10_out, and_11_out, and_12_out);
  xor xor_5 (S3, xor_1_out, or_2_out);
  xor xor_6 (S2, xor_2_out, or_3_out);
  xor xor_7 (S1, xor_3_out, or_4_out);
  xor xor_8 (S0, xor_4_out, C0);
endmodule
