// Logisim project 7.circ as structural Verilog: 1 circuit, main circuit main
module main (
  input  A3,
  input  A2,
  input  A1,
  input  A0,
  input  B3,
  input  B2,
  input  B1,
  input  B0,
  input  in_9,
  output out_10,
  output out_11,
  output out_12,
  output out_13,
  output out_14
);

  // _6_main main_1: pin names not known; wires that end beside it: A3, A2, A1, A0, B3, B2, B1, B0, out_10, in_9, out_11, out_12, out_13, out_14
endmodule
