// Logisim project 0.1.circ as structural Verilog: 1 circuit, main circuit main
module main (
  input  CLR,
  input  UP,
  input  DOWN,
  output y4,
  output y3,
  output y2,
  output y1
);

  wire and_1_out, and_2_out, and_3_out, and_4_out, and_5_out, and_6_out, and_7_out, and_8_out, and_9_out,
       and_10_out, and_11_out, and_12_out, and_13_out, and_14_out, and_15_out, and_16_out, and_17_out,
       and_18_out, and_19_out, and_20_out, and_21_out, and_22_out, and_23_out, and_24_out, and_25_out,
       and_26_out, d_ff_1_qn, d_ff_2_qn, d_ff_3_qn, d_ff_4_qn, nCLR_nUD_out, nCLRU_nD_out, not_1_out,
       not_2_out, not_3_out, not_4_out, not_5_out, not_6_out, or_1_out, or_2_out, or_3_out, or_4_out,
       or_5_out, or_6_out, or_7_out, or_8_out, or_9_out, or_10_out, or_11_out;

  or or_1 (or_1_out, CLR, UP, DOWN);
  not not_1 (not_1_out, or_1_out);
  not not_2 (not_2_out, not_1_out);
  not not_3 (not_3_out, CLR);
  not not_4 (not_4_out, DOWN);
  and nCLRU_nD (nCLRU_nD_out, not_3_out, not_4_out, UP);
  and and_1 (and_1_out, y4, d_ff_2_qn);
  and and_2 (and_2_out, y4, d_ff_3_qn);
  and and_3 (and_3_out, y4, y2, d_ff_4_qn);
  and and_4 (and_4_out, d_ff_1_qn, y2, y3, y1);
  not not_5 (not_5_out, CLR);
  not not_6 (not_6_out, UP);
  or or_2 (or_2_out, and_1_out, and_2_out, and_4_out, and_3_out);
  and nCLR_nUD (nCLR_nUD_out, DOWN, not_5_out, not_6_out);
  and and_5 (and_5_out, nCLRU_nD_out, or_2_out);
  and and_6 (and_6_out, y4, y3);
  and and_7 (and_7_out, y4, y2);
  and and_8 (and_8_out, y4, y1);
  and and_9 (and_9_out, d_ff_1_qn, d_ff_2_qn, d_ff_3_qn, d_ff_4_qn);
  or or_3 (or_3_out, and_6_out, and_7_out, and_8_out, and_9_out);
  and and_10 (and_10_out, nCLR_nUD_out, or_3_out);
  or or_4 (or_4_out, and_5_out, and_10_out);
  D_Flip_Flop d_ff_1 (.clk(not_2_out), .D(or_4_out), .Q(y4), .Qn(d_ff_1_qn));  // open: preset, en, reset
  and and_11 (and_11_out, y3, d_ff_3_qn);
  and and_12 (and_12_out, y3, d_ff_4_qn);
  and and_13 (and_13_out, d_ff_2_qn, y2, y1);
  or or_5 (or_5_out, and_11_out, and_12_out, and_13_out);
  and and_14 (and_14_out, nCLRU_nD_out, or_5_out);
  and and_15 (and_15_out, y3, y1);
  and and_16 (and_16_out, y3, y2);
  and and_17 (and_17_out, d_ff_2_qn, d_ff_3_qn, d_ff_4_qn);
  or or_6 (or_6_out, and_15_out, and_16_out, and_17_out);
  and and_18 (and_18_out, nCLR_nUD_out, or_6_out);
  or or_7 (or_7_out, and_14_out, and_18_out);
  D_Flip_Flop d_ff_2 (.clk(not_2_out), .D(or_7_out), .Q(y3), .Qn(d_ff_2_qn));  // open: preset, en, reset
  and and_19 (and_19_out, d_ff_3_qn, d_ff_4_qn);
  and and_20 (and_20_out, y2, y1);
  or or_8 (or_8_out, and_19_out, and_20_out);
  and and_21 (and_21_out, nCLR_nUD_out, or_8_out);
  and and_22 (and_22_out, d_ff_3_qn, y1);
  and and_23 (and_23_out, y2, d_ff_4_qn);
  or or_9 (or_9_out, and_22_out, and_23_out);
  or or_10 (or_10_out, and_21_out, and_24_out);
  and and_24 (and_24_out, nCLRU_nD_out, or_9_out);
  D_Flip_Flop d_ff_3 (.clk(not_2_out), .D(or_10_out), .Q(y2), .Qn(d_ff_3_qn));  // open: preset, en, reset
  and and_25 (and_25_out, d_ff_4_qn, nCLRU_nD_out);
  and and_26 (and_26_out, d_ff_4_qn, nCLR_nUD_out);
  D_Flip_Flop d_ff_4 (.clk(not_2_out), .D(or_11_out), .Q(y1), .Qn(d_ff_4_qn));  // open: preset, en, reset
  or or_11 (or_11_out, and_25_out, and_26_out);

  // Notes on the sheet:
  //   ————————————————————————————————————————————————————————————————————————————————
endmodule
