// Logisim project 0.circ as structural Verilog: 1 circuit, main circuit main
module main (
  input  CLR,
  input  C_plus,
  input  C_minus,
  output \本位 ,
  output \借位 ,
  output \进位 
);

  wire and_1_out, and_2_out, and_3_out, and_4_out, d_ff_1_q, d_ff_1_qn, not_1_out, not_2_out, not_3_out,
       not_4_out, not_5_out, not_6_out, not_8_out, not_9_out, not_11_out, not_12_out, or_1_out, or_2_out;

  not not_1 (not_1_out, CLR);
  not not_2 (not_2_out, C_plus);
  not not_3 (not_3_out, C_minus);
  not not_4 (not_4_out, or_1_out);
  or or_1 (or_1_out, CLR, C_minus, C_plus);
  and and_1 (and_1_out, d_ff_1_qn, not_1_out, not_2_out, C_minus);
  and and_2 (and_2_out, d_ff_1_qn, C_plus, not_3_out, not_1_out);
  and and_3 (and_3_out, not_2_out, C_minus, not_1_out, d_ff_1_q);
  and and_4 (and_4_out, C_plus, not_3_out, not_1_out, d_ff_1_qn);
  not not_5 (not_5_out, not_6_out);
  not not_6 (not_6_out, not_4_out);
  not not_7 (\借位 , not_8_out);
  not not_8 (not_8_out, and_3_out);
  not not_9 (not_9_out, and_4_out);
  not not_10 (\进位 , not_9_out);
  not not_11 (not_11_out, not_5_out);
  or or_2 (or_2_out, and_1_out, and_2_out);
  D_Flip_Flop d_ff_1 (.clk(not_11_out), .D(or_2_out), .Q(d_ff_1_q), .Qn(d_ff_1_qn));  // open: preset, en, reset
  not not_12 (not_12_out, d_ff_1_q);
  not not_13 (\本位 , not_12_out);
endmodule
