// Logisim project 1.circ as structural Verilog: 1 circuit, main circuit main
module main (
  output out_1,
  output out_2,
  output out_3,
  output out_4,
  output out_5,
  output out_6
);

  wire C_minus_out, C_plus_out, CLR_out, \main_2_借位 , \main_2_进位 , \main_3_借位 , \main_3_进位 ;

  Clock CLR (.out(CLR_out));
  Clock C_plus (.out(C_plus_out));
  Clock C_minus (.out(C_minus_out));
  _0_main main_1 (.\本位 (out_1), .CLR(CLR_out), .C_plus(\main_2_进位 ), .C_minus(\main_2_借位 ));  // open: 借位, 进位
  _0_main main_2 (
    .\本位 (out_2), .\借位 (\main_2_借位 ), .\进位 (\main_2_进位 ), .CLR(CLR_out), .C_plus(\main_3_进位 ),
    .C_minus(\main_3_借位 ));
  _0_main main_3 (.\本位 (out_3), .\借位 (\main_3_借位 ), .\进位 (\main_3_进位 ), .CLR(CLR_out), .C_plus(out_4), .C_minus(out_5));
  _0_main main_4 (.\本位 (out_6), .\借位 (out_5), .\进位 (out_4), .CLR(CLR_out), .C_plus(C_plus_out), .C_minus(C_minus_out));
  // _0_main main_5: pin names not known
endmodule
