// Logisim project 7_seg.circ as structural Verilog: 1 circuit, main circuit main
module main (
  input  A3,
  input  A2,
  input  A1,
  input  A0,
  output _1,
  output _2,
  output _3,
  output \_4_小数点 ,
  output _7,
  output _5,
  output _6,
  output _8
);

  wire and_1_out, and_2_out, and_3_out, and_4_out, and_5_out, and_6_out, and_7_out, and_8_out, and_9_out,
       and_10_out, and_11_out, and_12_out, and_13_out, and_14_out, and_15_out, and_16_out, and_17_out,
       not_1_out, not_2_out, not_3_out, not_4_out;

  not not_1 (not_1_out, A3);
  not not_2 (not_2_out, A2);
  not not_3 (not_3_out, A1);
  not not_4 (not_4_out, A0);
  and and_1 (and_1_out, not_1_out, A1, not_4_out);
  and and_2 (and_2_out, not_2_out, not_3_out, not_4_out);
  and and_3 (and_3_out, A1, not_4_out);
  or or_1 (_1, and_1_out, and_2_out);
  and and_4 (and_4_out, not_1_out, not_2_out, A1);
  and and_5 (and_5_out, A2, not_3_out);
  and and_6 (and_6_out, A1, not_4_out);
  and and_7 (and_7_out, not_1_out, not_2_out, A1);
  or or_2 (_5, A3, and_3_out, and_4_out, and_5_out);
  and and_8 (and_8_out, A2, not_3_out, A0);
  and and_9 (and_9_out, not_2_out, not_3_out, not_4_out);
  or or_3 (_2, and_6_out, and_8_out, and_9_out, and_7_out, A3);
  and and_10 (and_10_out, not_4_out, A1, A2);
  and and_11 (and_11_out, A2, not_3_out);
  and and_12 (and_12_out, not_3_out, not_4_out);
  nand nand_1 (_3, not_1_out, not_2_out, A1, not_4_out);
  or or_4 (_6, A3, and_10_out, and_11_out, and_12_out);
  and and_13 (and_13_out, not_2_out, not_3_out, not_4_out);
  and and_14 (and_14_out, A2, A0);
  or or_5 (_7, and_13_out, and_14_out, A1, A3);
  and and_15 (and_15_out, A1, A0);
  and and_16 (and_16_out, not_3_out, not_4_out);
  and and_17 (and_17_out, not_1_out, not_2_out);
  or or_6 (_8, A3, and_15_out, and_16_out, and_17_out);

  assign \_4_小数点  = 1'b0;
endmodule
