// Logisim project ALLL _封装.circ as structural Verilog: 1 circuit, main circuit main
module main (
  input  in_1,
  input  in_2,
  input  in_3,
  output out_4,
  output out_5,
  output out_6,
  output out_7,
  output out_8,
  output out_9,
  output out_10,
  output out_11,
  output out_12,
  output out_13,
  output out_14,
  output out_15,
  output out_16,
  output out_17,
  output out_18
);

  wire main_1_clr_2, main_1_down_2, main_1_up_2, main_2_out_5, main_2_out_6, main_2_out_7, main_2_out_8,
       main_2_out_9, main_2_out_10, main_2_out_11, main_2_out_12, main_3_y1, main_3_y2, main_3_y3, main_3_y4,
       \main_4__4_小数点 , \main_5__4_小数点 ;

  full_main main_1 (
    .CLR(in_1), .UP(in_2), .DOWN(in_3), .Y4(main_3_y4), .Y3(main_3_y3), .Y2(main_3_y2), .Y1(main_3_y1),
    .CLR_2(main_1_clr_2), .DOWN_2(main_1_down_2), .UP_2(main_1_up_2), .FULL(out_18));
  M2_main main_2 (
    .out_5(main_2_out_5), .out_6(main_2_out_6), .out_7(main_2_out_7), .out_8(main_2_out_8),
    .out_9(main_2_out_9), .out_10(main_2_out_10), .out_11(main_2_out_11), .out_12(main_2_out_12),
    .in_1(main_3_y4), .in_2(main_3_y3), .in_3(main_3_y2), .in_4(main_3_y1));
  _0_1_main main_3 (
    .y4(main_3_y4), .y3(main_3_y3), .y2(main_3_y2), .y1(main_3_y1), .CLR(main_1_clr_2), .UP(main_1_up_2),
    .DOWN(main_1_down_2));
  _7_seg_main main_4 (
    .A3(main_2_out_5), .A2(main_2_out_6), .A1(main_2_out_7), .A0(main_2_out_8), ._1(out_12), ._2(out_13),
    ._3(out_14), .\_4_小数点 (\main_4__4_小数点 ), ._7(out_6), ._5(out_4), ._6(out_5), ._8(out_7));
  _7_seg_main main_5 (
    .A3(main_2_out_9), .A2(main_2_out_10), .A1(main_2_out_11), .A0(main_2_out_12), ._1(out_15), ._2(out_16),
    ._3(out_17), .\_4_小数点 (\main_5__4_小数点 ), ._7(out_10), ._5(out_8), ._6(out_9), ._8(out_11));
  // also tied to GND on the sheet: {\main_4__4_小数点 , \main_5__4_小数点 }
endmodule
