// Logisim project ALLL.circ as structural Verilog: 1 circuit, main circuit main
module main (
);

  wire clock_1_out, clock_2_out, clock_3_out, main_1_clr_2, main_1_down_2, main_1_full, main_1_up_2,
       main_2_out_5, main_2_out_6, main_2_out_7, main_2_out_8, main_2_out_9, main_2_out_10, main_2_out_11,
       main_2_out_12, main_3_y1, main_3_y2, main_3_y3, main_3_y4, main_4__1, main_4__2, main_4__3,
       \main_4__4_小数点 , main_4__5, main_4__6, main_4__7, main_4__8, main_5__1, main_5__2, main_5__3,
       \main_5__4_小数点 , main_5__5, main_5__6, main_5__7, main_5__8;

  Clock clock_1 (.out(clock_1_out));
  Clock clock_2 (.out(clock_2_out));
  Clock clock_3 (.out(clock_3_out));
  full_main main_1 (
    .CLR(clock_1_out), .UP(clock_2_out), .DOWN(clock_3_out), .Y4(main_3_y4), .Y3(main_3_y3), .Y2(main_3_y2),
    .Y1(main_3_y1), .CLR_2(main_1_clr_2), .DOWN_2(main_1_down_2), .UP_2(main_1_up_2), .FULL(main_1_full));
  LED led_1 (.in(main_1_full));
  M2_main main_2 (
    .out_5(main_2_out_5), .out_6(main_2_out_6), .out_7(main_2_out_7), .out_8(main_2_out_8),
    .out_9(main_2_out_9), .out_10(main_2_out_10), .out_11(main_2_out_11), .out_12(main_2_out_12),
    .in_1(main_3_y4), .in_2(main_3_y3), .in_3(main_3_y2), .in_4(main_3_y1));
  _0_1_main main_3 (
    .y4(main_3_y4), .y3(main_3_y3), .y2(main_3_y2), .y1(main_3_y1), .CLR(main_1_clr_2), .UP(main_1_up_2),
    .DOWN(main_1_down_2));
  _7_Segment_Display u_7_segment_display_1 (
    .g(main_4__5), .f(main_4__6), .a(main_4__7), .b(main_4__8), .e(main_4__1), .d(main_4__2), .c(main_4__3),
    .dp(\main_4__4_小数点 ));
  _7_seg_main main_4 (
    .A3(main_2_out_5), .A2(main_2_out_6), .A1(main_2_out_7), .A0(main_2_out_8), ._1(main_4__1),
    ._2(main_4__2), ._3(main_4__3), .\_4_小数点 (\main_4__4_小数点 ), ._7(main_4__7), ._5(main_4__5),
    ._6(main_4__6), ._8(main_4__8));
  _7_Segment_Display u_7_segment_display_2 (
    .g(main_5__5), .f(main_5__6), .a(main_5__7), .b(main_5__8), .e(main_5__1), .d(main_5__2), .c(main_5__3),
    .dp(\main_5__4_小数点 ));
  _7_seg_main main_5 (
    .A3(main_2_out_9), .A2(main_2_out_10), .A1(main_2_out_11), .A0(main_2_out_12), ._1(main_5__1),
    ._2(main_5__2), ._3(main_5__3), .\_4_小数点 (\main_5__4_小数点 ), ._7(main_5__7), ._5(main_5__5),
    ._6(main_5__6), ._8(main_5__8));
endmodule
