// Logisim project F2TBCD测试.circ as structural Verilog: 1 circuit, main circuit main
module main (
  input  in_1,
  input  in_2,
  input  in_3,
  input  in_4,
  output out_5,
  output out_6,
  output out_7,
  output out_8,
  output out_9,
  output out_10,
  output out_11,
  output out_12
);

  M2_main main_1 (
    .out_5(out_5), .out_6(out_6), .out_7(out_7), .out_8(out_8), .out_9(out_9), .out_10(out_10),
    .out_11(out_11), .out_12(out_12), .in_1(in_1), .in_2(in_2), .in_3(in_3), .in_4(in_4));
endmodule
