// Logisim project M2.circ as structural Verilog: 1 circuit, main circuit main
module main (
  input  in_1,
  input  in_2,
  input  in_3,
  input  in_4,
  output out_5,
  output out_6,
  output out_7,
  output out_8,
  output out_9,
  output out_10,
  output out_11,
  output out_12
);

  wire and_1_out, main_2_c, or_1_out, or_2_out;

  \四位全加器_main  main_1 (
    .A3(1'b0), .B3(1'b0), .A2(1'b0), .B2(1'b0), .A1(1'b0), .B1(1'b0), .C0(main_2_c), .A0(1'b0), .B0(1'b0),
    .S3(out_5), .S2(out_6), .S1(out_7), .S0(out_8));  // open: C
  \四位全加器_main  main_2 (
    .A3(in_1), .B3(1'b0), .A2(in_2), .B2(or_1_out), .A1(in_3), .B1(or_1_out), .C0(1'b0), .A0(in_4),
    .B0(1'b0), .C(main_2_c), .S3(out_9), .S2(out_10), .S1(out_11), .S0(out_12));
  or or_1 (or_1_out, 1'b0, and_1_out);
  or or_2 (or_2_out, in_3, in_2);
  and and_1 (and_1_out, in_1, or_2_out);
endmodule
