// Logisim project full.circ as structural Verilog: 1 circuit, main circuit main
module main (
  input  CLR,
  input  UP,
  input  DOWN,
  input  Y4,
  input  Y3,
  input  Y2,
  input  Y1,
  output CLR_2,
  output DOWN_2,
  output UP_2,
  output FULL
);

  wire and_1_out, and_2_out, not_1_out, not_2_out, not_3_out, not_4_out, or_1_out, or_2_out;

  not not_1 (not_1_out, DOWN);
  and and_1 (and_1_out, Y4, Y3, Y2, Y1);
  not not_2 (not_2_out, and_1_out);
  or or_1 (or_1_out, CLR, UP, DOWN);
  and and_2 (and_2_out, Y4, Y3, not_1_out, Y2, Y1);
  and and_3 (UP_2, not_2_out, UP);
  not not_3 (not_3_out, or_1_out);
  not not_4 (not_4_out, not_3_out);
  D_Flip_Flop d_ff_1 (.clk(not_4_out), .D(and_2_out), .Q(FULL));  // open: Qn, preset, en, reset
  or or_2 (or_2_out, Y1, Y2, Y3, Y4);
  and and_4 (DOWN_2, DOWN, or_2_out);

  assign CLR_2 = CLR;
endmodule
