// Logisim project 七段数码管显示.circ as structural Verilog: 1 circuit, main circuit main
module main (
  input  in_1,
  input  in_2,
  input  in_3,
  input  in_4
);

  wire main_1__1, main_1__2, main_1__3, \main_1__4_小数点 , main_1__5, main_1__6, main_1__7, main_1__8;

  _7_Segment_Display u_7_segment_display_1 (
    .g(main_1__5), .f(main_1__6), .a(main_1__7), .b(main_1__8), .e(main_1__1), .d(main_1__2), .c(main_1__3),
    .dp(\main_1__4_小数点 ));
  _7_seg_main main_1 (
    .A3(in_1), .A2(in_2), .A1(in_3), .A0(in_4), ._1(main_1__1), ._2(main_1__2), ._3(main_1__3),
    .\_4_小数点 (\main_1__4_小数点 ), ._7(main_1__7), ._5(main_1__5), ._6(main_1__6), ._8(main_1__8));
endmodule
