// Logisim project 最终测试.circ as structural Verilog: 1 circuit, main circuit main
module main (
);

  wire clock_1_out, clock_2_out, clock_3_out, main_1_out_4, main_1_out_5, main_1_out_6, main_1_out_7,
       main_1_out_8, main_1_out_9, main_1_out_10, main_1_out_11, main_1_out_12, main_1_out_13, main_1_out_14,
       main_1_out_15, main_1_out_16, main_1_out_17, main_1_out_18;

  Clock clock_1 (.out(clock_1_out));
  Clock clock_2 (.out(clock_2_out));
  Clock clock_3 (.out(clock_3_out));
  _7_Segment_Display u_7_segment_display_1 (
    .g(main_1_out_4), .f(main_1_out_5), .a(main_1_out_6), .b(main_1_out_7), .e(main_1_out_12),
    .d(main_1_out_13), .c(main_1_out_14));  // open: dp
  \ALLL__封装_main  main_1 (
    .in_1(clock_1_out), .in_2(clock_2_out), .in_3(clock_3_out), .out_4(main_1_out_4), .out_5(main_1_out_5),
    .out_6(main_1_out_6), .out_7(main_1_out_7), .out_8(main_1_out_8), .out_9(main_1_out_9),
    .out_10(main_1_out_10), .out_11(main_1_out_11), .out_12(main_1_out_12), .out_13(main_1_out_13),
    .out_14(main_1_out_14), .out_15(main_1_out_15), .out_16(main_1_out_16), .out_17(main_1_out_17),
    .out_18(main_1_out_18));
  _7_Segment_Display u_7_segment_display_2 (
    .g(main_1_out_8), .f(main_1_out_9), .a(main_1_out_10), .b(main_1_out_11), .e(main_1_out_15),
    .d(main_1_out_16), .c(main_1_out_17));  // open: dp
  LED led_1 (.in(main_1_out_18));
endmodule
