// Logisim project 计数器应用.circ as structural Verilog: 1 circuit, main circuit main
module main (
  output out_1,
  output out_2,
  output out_3,
  output out_4
);

  wire clock_1_out, clock_2_out, clock_3_out;

  Clock clock_1 (.out(clock_1_out));
  Clock clock_2 (.out(clock_2_out));
  Clock clock_3 (.out(clock_3_out));
  _0_1_main main_1 (
    .y4(out_1), .y3(out_2), .y2(out_3), .y1(out_4), .CLR(clock_1_out), .UP(clock_2_out), .DOWN(clock_3_out));
endmodule
